# Fritzing sketch Derevyaka (saved by Fritzing 0.9.3b)

parts:
  GLCD_128x1 = 128 x 64 Graphic LCD
  Часть1 = Arduino Uno (Rev3)
  Часть2 = Arduino Uno (Rev3)
  J1 = Infrared Proximity Sensor
  J2 = Infrared Proximity Sensor
  Часть3 = LED Matrix - Serial Interface - Red/Green/Blue
  Часть4 = LED Matrix - Serial Interface - Red/Green/Blue
  Часть5 = RFID-RC522-v2
  Часть6 = Arduino Uno (Rev3)
  Pololu_A1 = Pololu A4988 [package=SO16]
  M1 = Stepper Motor - Bipolar  # not connected
  M2 = Stepper Motor - Bipolar  # not connected
  Pololu_A2 = Pololu A4988 [package=SO16]
  M3 = ps2 gamepad [package=THT]
  hc-sr1 = hc-sr04
  J3 = Infrared Proximity Sensor
  J4 = Infrared Proximity Sensor
  S1 = Pushbutton [package="[THT]"]
  S2 = Pushbutton [package="[THT]"]
  S3 = Pushbutton [package="[THT]"]
  MP3-1 = Serial MP3 Player
  R1 = Resistor [tolerance=±5% resistance=220 package=THT]  # not connected
  R2 = Resistor [tolerance=±5% resistance=220 package=THT]
  R3 = Resistor [tolerance=±5% resistance=220 package=THT]

nets:
  GND: GLCD_128x1.1_Vss, GLCD_128x1.15_CS1, GLCD_128x1.20_K(-), Часть1.GND, Часть2.GND, J1.GND, J2.GND, Часть3.GND, Часть4.GND, Часть5.GND, Часть6.GND, Pololu_A1.GND, Pololu_A2.GND, M3.GND, hc-sr1.GND, J3.GND, J4.GND, MP3-1.pin1, R2.Pin_1, R3.Pin_1
  VCC: GLCD_128x1.2_Vdd, GLCD_128x1.19_A(+), Часть1.5V, Часть5.3_3V, hc-sr1.VCC, J3.Vcc, J4.Vcc, S1.Pin_3, S1.Pin_4, S2.Pin_3, S2.Pin_4, S3.Pin_3, S3.Pin_4
  N1: GLCD_128x1.4_D/I, Часть1.D8
  N2: GLCD_128x1.5_R/W, Часть1.D9_PWM
  N3: GLCD_128x1.6_Enable, Часть1.D3_PWM
  N4: Часть1.A0, S1.Pin_2
  N5: Часть1.A1, S2.Pin_2
  N6: Часть1.A2, S3.Pin_2
  N7: Часть1.D10_PWM/SS, Часть5.SDA
  N8: Часть1.D11_PWM/MOSI, Часть5.MOSI
  N9: Часть1.D12/MISO, Часть5.MISO
  N10: Часть1.D13/SCK, Часть5.SCK
  N11: Часть1.A4/SDA, Часть2.A4/SDA, Часть6.A4/SDA
  N12: Часть1.A5/SCL, Часть2.A5/SCL, Часть6.A5/SCL
  N13: Часть1.D2, J4.Vout
  N14: Часть1.D4, Часть5.RST
  N15: Часть1.D5_PWM, J3.Vout
  N16: Часть1.D6_PWM, hc-sr1.Trig
  N17: Часть1.D7, hc-sr1.Echo
  N18: Часть2.D9_PWM, Часть3.CS, Часть4.CS
  N19: Часть2.D11_PWM/MOSI, Часть3.MOSI
  N20: Часть2.D13/SCK, Часть3.SCK, Часть4.SCK
  N21: Часть2.D2, MP3-1.pin3
  N22: Часть2.D3_PWM, MP3-1.pin4
  N23: Часть2.D4, J2.Vout
  N24: Часть2.D5_PWM, J1.Vout
  VCC_2: Часть2.5V, J1.Vcc, J2.Vcc, Часть3.VCC, Часть4.VCC, MP3-1.pin2
  N25: Часть3.MISO, Часть4.MOSI
  N26: Часть6.D8, M3.DAT
  N27: Часть6.D10_PWM/SS, Pololu_A1.STEP
  N28: Часть6.D11_PWM/MOSI, Pololu_A2.STEP
  N29: Часть6.D12/MISO, Pololu_A1.DIR
  N30: Часть6.D13/SCK, Pololu_A2.DIR
  N31: Часть6.D4, M3.CLK
  N32: Часть6.D6_PWM, M3.ATT
  N33: Часть6.D7, M3.CMD
  VDD: Часть6.5V, Pololu_A1.VDD, Pololu_A2.VDD, M3.3.3V

custom parts:
  RFID-RC522-v2: A simple China made RFID-RC522 Reader; do check the pin labels, as this is a MFRC522 based clone.
  ps2 gamepad: PS2 gamepad. Warning! PCB view is designed for the female connector available from https://www.robotshop.com/en/ps2-connector.html. However there is no mechanical information that I can find so ipcb was generated from a scaled jpg and may well be wrong. Print the footprint out and check it against a real part before ordering boards!
  Serial MP3 Player: The module is a kind of simple MP3 player device which is based on a high-quality MP3 audio chip---YX5300. It can support 8k Hz ~ 48k Hz sampling frequency MP3 and WAV file formats. There is a TF card socket on board, so you can plug the micro SD card that stores audio files. MCU can control the MP3 playback state by sending commands to the module via UART port, such as switch songs, change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
